# Fritzing sketch bipolar-stepper (saved by Fritzing 0.9.9b)
breadboards: 1

parts:
  Part1 = Arduino Uno (Rev3)
  RE1 = Rotary Encoder [package=THT]
  L298N1 = L298N DC motor driver
  M1 = Stepper Motor - Bipolar  # not connected

nets:
  N1: Part1.D8, L298N1.IN1
  N2: Part1.D9_PWM, L298N1.IN2
  N3: Part1.D10_PWM/SS, L298N1.IN3
  N4: Part1.D11_PWM/MOSI, L298N1.IN4
  N5: Part1.GND, RE1.EncoderPinC
  N6: Part1.D2, RE1.EncoderPinB
  N7: Part1.D3_PWM, RE1.EncoderPinA

custom parts:
  L298N DC motor driver: 2x DC motor driver with 78M05 positive voltage regulator (7..35 V) L298N: max 46 V, 2 A Set 5 V Enable jumper to enable 5 V regultor (needed for the L298N) and +5 V output at screw terminal or supply external +5 V at screw terminal Set ENA and/or ENB to +5 V to enable motor permanently or supply ENA and/or ENB with PWM signal IN1 and IN2 set rotation directory for motor A (OUT1/OUT2) IN2 and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
